// Logisim project GROUP9MultiCycleCpu.circ as structural Verilog: 6 circuits, main circuit main
module main (
  input  RAM_RESET,
  input  RESET,
  output out_3,
  output out_4
);

  wire clock_1_out, control_unit_1_ain, control_unit_1_aluop, control_unit_1_bin, control_unit_1_done,
       control_unit_1_irin, control_unit_1_r_xout, control_unit_1_r_yout, demultiplexer_2_out0,
       demultiplexer_2_out1, demultiplexer_2_out2, demultiplexer_2_out3, demultiplexer_2_out4,
       demultiplexer_2_out5, demultiplexer_2_out6, demultiplexer_2_out7, or_1_out, or_2_out, or_3_out;
  wire [1:0] control_unit_1_asen;
  wire [2:0] multiplexer_3_out, n3_bit_counter_1_counter, register_1_q, register_1_q_3;
  wire [3:0] register_file_1_out_19, register_file_1_out_19_2, register_file_1_out_20,
       register_file_1_out_20_2, register_file_1_out_21, register_file_1_out_21_2, register_file_1_out_22,
       register_file_1_out_23, register_file_1_out_23_2, register_file_1_out_24, register_file_1_out_24_2,
       register_file_1_out_25, register_file_1_out_25_2;
  wire [7:0] alu_1_out_4, demultiplexer_1_out0, demultiplexer_1_out1, demultiplexer_1_out2,
       demultiplexer_1_out3, demultiplexer_1_out4, demultiplexer_1_out5, demultiplexer_1_out6,
       demultiplexer_1_out7, multiplexer_1_out, multiplexer_2_out, ram_1_data, register_2_q, register_3_q,
       register_file_1_out_26;
  wire [7:4] register_file_1_out_22_2;
  wire [7:6] register_1_q_2;

  _3_bit_Counter u_3_bit_counter_1 (
    .CLK(clock_1_out), .EN(or_1_out), .COUNTER(n3_bit_counter_1_counter), .RESET(RESET));
  Clock clock_1 (.out(clock_1_out));
  RAM #(.addrWidth(3)) ram_1 (
    .addr(n3_bit_counter_1_counter), .data(ram_1_data), .ld(or_1_out), .clr(RAM_RESET));  // open: sel, clk
  or or_1 (or_1_out, control_unit_1_asen[1], control_unit_1_irin);
  Hex_Digit_Display hex_digit_display_1 (.value(register_file_1_out_19_2));  // open: dp
  Hex_Digit_Display hex_digit_display_2 (.value(register_file_1_out_19));  // open: dp
  Multiplexer #(.select(2), .width(8)) multiplexer_1 (
    .in0(multiplexer_2_out), .in1(register_3_q), .in2(ram_1_data), .out(multiplexer_1_out),
    .sel(control_unit_1_asen), .en(control_unit_1_done));  // open: in3
  Hex_Digit_Display hex_digit_display_3 (.value(register_file_1_out_20_2));  // open: dp
  Demultiplexer #(.select(3), .width(8)) demultiplexer_1 (
    .out0(demultiplexer_1_out0), .out1(demultiplexer_1_out1), .out2(demultiplexer_1_out2),
    .out3(demultiplexer_1_out3), .out4(demultiplexer_1_out4), .out5(demultiplexer_1_out5),
    .out6(demultiplexer_1_out6), .out7(demultiplexer_1_out7), .in(multiplexer_1_out), .sel(register_1_q),
    .en(control_unit_1_done));
  Hex_Digit_Display hex_digit_display_4 (.value(register_file_1_out_20));  // open: dp
  Demultiplexer #(.select(3)) demultiplexer_2 (
    .out0(demultiplexer_2_out0), .out1(demultiplexer_2_out1), .out2(demultiplexer_2_out2),
    .out3(demultiplexer_2_out3), .out4(demultiplexer_2_out4), .out5(demultiplexer_2_out5),
    .out6(demultiplexer_2_out6), .out7(demultiplexer_2_out7), .sel(register_1_q), .en(control_unit_1_done));  // open: in
  Hex_Digit_Display hex_digit_display_5 (.value(register_file_1_out_21_2));  // open: dp
  Hex_Digit_Display hex_digit_display_6 (.value(register_file_1_out_21));  // open: dp
  Register_File register_file_1 (
    .in_1(demultiplexer_1_out0), .in_3(demultiplexer_1_out1), .in_5(demultiplexer_1_out2),
    .in_7(demultiplexer_1_out3), .in_9(demultiplexer_1_out4), .in_11(demultiplexer_1_out5),
    .in_13(demultiplexer_1_out6), .in_15(demultiplexer_1_out7), .in_17(clock_1_out), .in_18(RESET),
    .out_19({register_file_1_out_19_2, register_file_1_out_19}),
    .out_20({register_file_1_out_20_2, register_file_1_out_20}),
    .out_21({register_file_1_out_21_2, register_file_1_out_21}),
    .out_22({register_file_1_out_22_2, register_file_1_out_22}),
    .out_23({register_file_1_out_23_2, register_file_1_out_23}),
    .out_24({register_file_1_out_24_2, register_file_1_out_24}),
    .out_25({register_file_1_out_25_2, register_file_1_out_25}), .out_26(register_file_1_out_26),
    .in_2(demultiplexer_2_out0), .in_4(demultiplexer_2_out1), .in_6(demultiplexer_2_out2),
    .in_8(demultiplexer_2_out3), .in_10(demultiplexer_2_out4), .in_12(demultiplexer_2_out5),
    .in_14(demultiplexer_2_out6), .in_16(demultiplexer_2_out7));
  Register register_1 (
    .D(ram_1_data), .en(control_unit_1_irin), .Q({register_1_q_2, register_1_q, register_1_q_3}),
    .clk(clock_1_out), .clr(RESET));
  Hex_Digit_Display hex_digit_display_7 (.value(register_file_1_out_22_2));  // open: dp
  Hex_Digit_Display hex_digit_display_8 (.value(register_file_1_out_22));  // open: dp
  Multiplexer #(.select(3), .width(8)) multiplexer_2 (
    .in0({register_file_1_out_19_2, register_file_1_out_19}),
    .in1({register_file_1_out_20_2, register_file_1_out_20}),
    .in2({register_file_1_out_21_2, register_file_1_out_21}),
    .in3({register_file_1_out_22_2, register_file_1_out_22}),
    .in4({register_file_1_out_23_2, register_file_1_out_23}),
    .in5({register_file_1_out_24_2, register_file_1_out_24}),
    .in6({register_file_1_out_25_2, register_file_1_out_25}), .in7(register_file_1_out_26),
    .out(multiplexer_2_out), .sel(multiplexer_3_out), .en(or_3_out));
  or or_2 (or_2_out, RESET, control_unit_1_done);
  Hex_Digit_Display hex_digit_display_9 (.value(register_file_1_out_23_2));  // open: dp
  _2_bit_counter u_2_bit_counter_1 (.MSB(out_3), .LSB(out_4), .CLK(clock_1_out), .Done(or_2_out));
  Hex_Digit_Display hex_digit_display_10 (.value(register_file_1_out_23));  // open: dp
  Hex_Digit_Display hex_digit_display_11 (.value(register_file_1_out_24_2));  // open: dp
  Multiplexer #(.width(3)) multiplexer_3 (
    .in0(register_1_q_3), .in1(register_1_q), .out(multiplexer_3_out), .sel(control_unit_1_r_xout));  // open: en
  Hex_Digit_Display hex_digit_display_12 (.value(register_file_1_out_24));  // open: dp
  Register register_2 (
    .D(multiplexer_2_out), .en(control_unit_1_ain), .Q(register_2_q), .clk(clock_1_out), .clr(RESET));
  Control_Unit control_unit_1 (
    .OP1(register_1_q_2[7]), .OP0(register_1_q_2[6]), .Q1___MSB(out_3), .Q0___LSB(out_4),
    .Asen(control_unit_1_asen[0]), .ALUop(control_unit_1_aluop), .R_Xout(control_unit_1_r_xout),
    .R_Yout(control_unit_1_r_yout), .DINout(control_unit_1_asen[1]), .Ain(control_unit_1_ain),
    .Bin(control_unit_1_bin), .IRin(control_unit_1_irin), .Done(control_unit_1_done));
  Hex_Digit_Display hex_digit_display_13 (.value(register_file_1_out_25_2));  // open: dp
  Hex_Digit_Display hex_digit_display_14 (.value(register_file_1_out_25));  // open: dp
  or or_3 (or_3_out, control_unit_1_r_xout, control_unit_1_r_yout);
  Hex_Digit_Display hex_digit_display_15 (.value(register_file_1_out_26[7:4]));  // open: dp
  Hex_Digit_Display hex_digit_display_16 (.value(register_file_1_out_26[3:0]));  // open: dp
  ALU alu_1 (.Register_A(multiplexer_2_out), .Bus(register_2_q), .out_4(alu_1_out_4), .ALUop(control_unit_1_aluop));
  Register register_3 (.D(alu_1_out_4), .en(control_unit_1_bin), .Q(register_3_q), .clk(clock_1_out), .clr(RESET));

  // Notes on the sheet:
  //   CLK
  //   R0
  //   R1
  //   R2
  //   IR
  //   R3
  //   R4
  //   RY
  //   RX
  //   R5
  //   Register A
  //   R6
  //   R7
  //   Register B
endmodule

module ALU (
  input  [7:0] Register_A,
  input  [7:0] Bus,
  input  ALUop,
  output [7:0] out_4
);

  wire [7:0] xor_1_out;

  xor xor_1 (xor_1_out[0], Bus[0], ALUop);
  xor xor_2 (xor_1_out[1], Bus[1], ALUop);
  xor xor_3 (xor_1_out[2], Bus[2], ALUop);
  xor xor_4 (xor_1_out[3], Bus[3], ALUop);
  xor xor_5 (xor_1_out[4], Bus[4], ALUop);
  xor xor_6 (xor_1_out[5], Bus[5], ALUop);
  xor xor_7 (xor_1_out[6], Bus[6], ALUop);
  xor xor_8 (xor_1_out[7], Bus[7], ALUop);
  Adder adder_1 (.a(Register_A), .b(xor_1_out), .out(out_4), .cin(ALUop));  // open: cout

  // Notes on the sheet:
  //   Output -> Register B
endmodule

module _2_bit_counter (
  input  CLK,
  input  Done,
  output MSB,
  output LSB
);

  wire and_1_out, and_2_out, not_1_out, not_2_out, xor_1_out;

  not not_1 (not_1_out, LSB);
  not not_2 (not_2_out, Done);
  and and_1 (and_1_out, not_1_out, not_2_out);
  and and_2 (and_2_out, not_2_out, xor_1_out);
  D_Flip_Flop d_ff_1 (.clk(CLK), .D(and_1_out), .Q(LSB));  // open: Qn, preset, en, reset
  D_Flip_Flop d_ff_2 (.clk(CLK), .D(and_2_out), .Q(MSB));  // open: Qn, preset, en, reset
  xor xor_1 (xor_1_out, MSB, LSB);
endmodule

module Register_File (
  input  [7:0] in_1,
  input  in_2,
  input  [7:0] in_3,
  input  in_4,
  input  [7:0] in_5,
  input  in_6,
  input  [7:0] in_7,
  input  in_8,
  input  [7:0] in_9,
  input  in_10,
  input  [7:0] in_11,
  input  in_12,
  input  [7:0] in_13,
  input  in_14,
  input  [7:0] in_15,
  input  in_16,
  input  in_17,
  input  in_18,
  output [7:0] out_19,
  output [7:0] out_20,
  output [7:0] out_21,
  output [7:0] out_22,
  output [7:0] out_23,
  output [7:0] out_24,
  output [7:0] out_25,
  output [7:0] out_26
);

  Register register_1 (.D(in_1), .en(in_2), .Q(out_19), .clk(in_17), .clr(in_18));
  Register register_2 (.D(in_3), .en(in_4), .Q(out_20), .clk(in_17), .clr(in_18));
  Register register_3 (.D(in_5), .en(in_6), .Q(out_21), .clk(in_17), .clr(in_18));
  Register register_4 (.D(in_7), .en(in_8), .Q(out_22), .clk(in_17), .clr(in_18));
  Register register_5 (.D(in_9), .en(in_10), .Q(out_23), .clk(in_17), .clr(in_18));
  Register register_6 (.D(in_11), .en(in_12), .Q(out_24), .clk(in_17), .clr(in_18));
  Register register_7 (.D(in_13), .en(in_14), .Q(out_25), .clk(in_17), .clr(in_18));
  Register register_8 (.D(in_15), .en(in_16), .Q(out_26), .clk(in_17), .clr(in_18));

  // Notes on the sheet:
  //   R0
  //   R1
  //   R2
  //   R3
  //   R4
  //   R5
  //   R6
  //   R7
endmodule

module Control_Unit (
  input  OP1,
  input  OP0,
  input  Q1___MSB,
  input  Q0___LSB,
  output Asen,
  output ALUop,
  output R_Xout,
  output R_Yout,
  output Done,
  output DINout,
  output Ain,
  output Bin,
  output IRin
);

  wire and_1_out, and_2_out, and_3_out, and_4_out, and_6_out, and_7_out, and_8_out, and_9_out, and_10_out,
       and_11_out, and_12_out, not_1_out, not_2_out, not_3_out, not_4_out, or_1_out, or_3_out;

  not not_1 (not_1_out, OP0);
  not not_2 (not_2_out, OP1);
  not not_3 (not_3_out, Q0___LSB);
  and and_1 (and_1_out, not_1_out, not_2_out);
  and and_2 (and_2_out, OP0, not_2_out);
  and and_3 (and_3_out, not_1_out, OP1);
  and and_4 (and_4_out, OP0, OP1);
  not not_4 (not_4_out, Q1___MSB);
  or or_1 (or_1_out, and_3_out, and_4_out);
  and and_5 (IRin, not_4_out, not_3_out);
  and and_6 (and_6_out, not_4_out, Q0___LSB);
  and and_7 (and_7_out, not_3_out, Q1___MSB);
  and and_8 (and_8_out, Q1___MSB, Q0___LSB);
  and and_9 (and_9_out, and_1_out, and_7_out);
  and and_10 (and_10_out, and_2_out, and_7_out);
  and and_11 (and_11_out, or_1_out, and_8_out);
  and and_12 (and_12_out, or_1_out, and_6_out);
  and and_13 (R_Xout, or_1_out, and_7_out);
  or or_2 (R_Yout, and_12_out, and_9_out);
  or or_3 (or_3_out, and_9_out, and_10_out);
  and and_14 (DINout, and_10_out, and_7_out);
  or or_4 (Done, or_3_out, and_11_out);
  and and_15 (Ain, or_1_out, and_6_out);
  and and_16 (Bin, or_1_out, and_7_out);

  assign ALUop = OP0;
  assign Asen = OP1;

  // Notes on the sheet:
  //   OPERATION CHECK + DONE SIGNAL
  //   mv
  //   mvi
  //   add
  //   sub
  //   COUNTER CHECK
  //   T0
  //   T1
  //   T2
  //   T3
  //   BUS CHECK
  //   WRITE CHECK
  //   ALU
endmodule

module _3_bit_Counter (
  input  CLK,
  input  EN,
  input  RESET,
  output [2:0] COUNTER
);

  wire and_1_out, not_1_out, xor_1_out, xor_2_out;

  not not_1 (not_1_out, COUNTER[0]);
  D_Flip_Flop d_ff_1 (.clk(CLK), .D(not_1_out), .Q(COUNTER[0]), .en(EN), .reset(RESET));  // open: Qn, preset
  D_Flip_Flop d_ff_2 (.clk(CLK), .D(xor_1_out), .Q(COUNTER[1]), .en(EN), .reset(RESET));  // open: Qn, preset
  D_Flip_Flop d_ff_3 (.clk(CLK), .D(xor_2_out), .Q(COUNTER[2]), .en(EN), .reset(RESET));  // open: Qn, preset
  xor xor_1 (xor_1_out, COUNTER[0], COUNTER[1]);
  and and_1 (and_1_out, COUNTER[0], COUNTER[1]);
  xor xor_2 (xor_2_out, and_1_out, COUNTER[2]);
endmodule
