// Logisim project multi-cycle cpu.circ as structural Verilog: 4 circuits, main circuit main
// Control Logic
module main (
  input  [7:0] DIN,
  input  in_2,
  input  Ain,
  input  Asen,
  input  Bin,
  output DIN_out,
  output Bout,
  output [2:0] R0__R7_out,
  output IRin
);

  wire clock_1_out, control_logic_1_ryout, decoder_1_out0, decoder_1_out1, decoder_1_out2, decoder_1_out3,
       decoder_1_out4, decoder_1_out5, decoder_1_out6, decoder_1_out7, n2_bit_counter_1_t0,
       n2_bit_counter_1_t1, n2_bit_counter_1_t2, n2_bit_counter_1_t3, pull_resistor_1_node;
  wire [1:0] IR_q_3;
  wire [2:0] IR_q, IR_q_2;
  wire [7:0] A_q, alu_1_result, B_q, multiplexer_1_out, multiplexer_2_out, multiplexer_3_out, R0_q, R1_q,
       R2_q, R3_q, R4_q, R5_q, R6_q, R7_q;

  Clock clock_1 (.out(clock_1_out));
  Register R0 (.D(multiplexer_3_out), .en(decoder_1_out0), .Q(R0_q), .clk(clock_1_out));  // open: clr
  Register R1 (.D(multiplexer_3_out), .en(decoder_1_out1), .Q(R1_q), .clk(clock_1_out));  // open: clr
  Register R2 (.D(multiplexer_3_out), .en(decoder_1_out2), .Q(R2_q), .clk(clock_1_out));  // open: clr
  Register R3 (.D(multiplexer_3_out), .en(decoder_1_out3), .Q(R3_q), .clk(clock_1_out));  // open: clr
  Register R4 (.D(multiplexer_3_out), .en(decoder_1_out4), .Q(R4_q), .clk(clock_1_out));  // open: clr
  Register R5 (.D(multiplexer_3_out), .en(decoder_1_out5), .Q(R5_q), .clk(clock_1_out));  // open: clr
  Register R6 (.D(multiplexer_3_out), .en(decoder_1_out6), .Q(R6_q), .clk(clock_1_out));  // open: clr
  Register R7 (.D(multiplexer_3_out), .en(decoder_1_out7), .Q(R7_q), .clk(clock_1_out));  // open: clr
  Register A (.D(multiplexer_3_out), .en(Ain), .Q(A_q), .clk(clock_1_out));  // open: clr
  ALU alu_1 (.A(A_q), .Bus(multiplexer_3_out), .Asen(Asen), .Result(alu_1_result));
  Multiplexer #(.select(3), .width(8)) multiplexer_1 (
    .in0(R0_q), .in1(R1_q), .in2(R2_q), .in3(R3_q), .in4(R4_q), .in5(R5_q), .in6(R6_q), .in7(R7_q),
    .out(multiplexer_1_out), .sel(R0__R7_out));  // open: en
  Register B (.D(alu_1_result), .en(Bin), .Q(B_q), .clk(clock_1_out));  // open: clr
  Multiplexer #(.width(8)) multiplexer_2 (
    .in0(multiplexer_1_out), .in1(B_q), .out(multiplexer_2_out), .sel(Bout));  // open: en
  Register IR (.D(DIN), .en(IRin), .Q({IR_q_3, IR_q_2, IR_q}), .clk(clock_1_out));  // open: clr
  Multiplexer #(.width(8)) multiplexer_3 (
    .in0(multiplexer_2_out), .in1(DIN), .out(multiplexer_3_out), .sel(DIN_out));  // open: en
  _2_bit_Counter u_2_bit_counter_1 (
    .in_1(in_2), .CLK(clock_1_out), .T0(n2_bit_counter_1_t0), .T1(n2_bit_counter_1_t1),
    .T2(n2_bit_counter_1_t2), .T3(n2_bit_counter_1_t3));  // open: Clear
  Multiplexer #(.width(3)) multiplexer_4 (
    .in0(IR_q_2), .in1(IR_q), .out(R0__R7_out), .en(control_logic_1_ryout));  // open: sel
  Decoder #(.select(3)) decoder_1 (
    .out0(decoder_1_out0), .out1(decoder_1_out1), .out2(decoder_1_out2), .out3(decoder_1_out3),
    .out4(decoder_1_out4), .out5(decoder_1_out5), .out6(decoder_1_out6), .out7(decoder_1_out7), .sel(IR_q_2));  // open: en
  Pull_Resistor pull_resistor_1 (.node(pull_resistor_1_node));
  Control_Logic control_logic_1 (
    .T0(n2_bit_counter_1_t0), .T1(n2_bit_counter_1_t1), .T2(n2_bit_counter_1_t2), .T3(n2_bit_counter_1_t3),
    .LSB_Op0(IR_q_3[0]), .MSB_Op1(IR_q_3[1]), .IRin(IRin), .DINout(DIN_out), .Ain(Ain), .Bin(Bin),
    .Ryout(control_logic_1_ryout), .Asen(Asen), .Rxin_and_Done(pull_resistor_1_node), .Bout(Bout));

  // Notes on the sheet:
  //   Rx
  //   Ry
endmodule

module ALU (
  input  [7:0] A,
  input  [7:0] Bus,
  input  Asen,
  output [7:0] Result
);

  wire [7:0] adder_1_out, subtractor_1_out;

  Adder adder_1 (.a(A), .b(Bus), .out(adder_1_out));  // open: cin, cout
  Subtractor subtractor_1 (.a(A), .b(Bus), .out(subtractor_1_out));  // open: bin, bout
  Multiplexer #(.width(8)) multiplexer_1 (
    .in0(adder_1_out), .in1(subtractor_1_out), .out(Result), .sel(Asen));  // open: en
endmodule

module _2_bit_Counter (
  input  in_1,
  input  Clear,
  input  CLK,
  output T0,
  output T1,
  output T2,
  output T3
);

  wire [1:0] counter_1_q;

  Counter #(.width(2), .max('h3)) counter_1 (
    .count(in_1), .Q(counter_1_q), .clk(CLK), .clr(Clear));  // open: load, D, carry
  Decoder #(.select(2)) decoder_1 (.out0(T0), .out1(T1), .out2(T2), .out3(T3), .sel(counter_1_q));  // open: en
endmodule

module Control_Logic (
  input  T0,
  input  T1,
  input  T2,
  input  T3,
  input  LSB_Op0,
  input  MSB_Op1,
  output IRin,
  output DINout,
  output Ain,
  output Bin,
  output Ryout,
  output Asen,
  output Rxin_and_Done,
  output Bout
);

  wire add, and_6_out, and_7_out, mv, mvi, or_1_out, or_2_out, sub;

  Decoder #(.select(2), .enable("false")) decoder_1 (
    .out0(mv), .out1(mvi), .out2(add), .out3(sub), .sel({MSB_Op1, LSB_Op0}));
  and and_1 (DINout, T1, mvi);
  or or_1 (or_1_out, mv, mvi);
  or or_2 (or_2_out, add, sub);
  and and_2 (Ain, T1, or_2_out);
  and and_3 (Bin, T2, or_2_out);
  and and_4 (Asen, sub, T2);
  and and_5 (Bout, or_2_out, T3);
  and and_6 (and_6_out, T1, mv);
  and and_7 (and_7_out, T1, or_1_out);
  or or_3 (Ryout, and_6_out, Bin);
  or or_4 (Rxin_and_Done, and_7_out, Bout);

  assign IRin = T0;
endmodule
